# Fritzing sketch Schematic (saved by Fritzing 0.9.3b)
breadboards: 1

parts:
  Raspberry_Pi_1 = Raspberry Pi 3 [part_number=RPI-3-V1.2]
  S1 = Pushbutton [package="[THT]"]
  S2 = Pushbutton [package="[THT]"]
  C1 = Ceramic Capacitor [capacitance=100nF package="100 mil [THT, multilayer]"]
  R1 = Resistor [tolerance=±5% resistance=13k package=THT]
  R2 = Resistor [tolerance=±5% resistance=13k package=THT]
  R3 = Resistor [tolerance=±5% resistance=13k package=THT]
  LED4 = LED - 5mm [color="Orange (620nm)" package="5 mm [THT]"]
  R4 = Resistor [tolerance=±5% resistance=13k package=THT]
  R5 = Resistor [tolerance=±5% resistance=13k package=THT]
  R6 = Resistor [tolerance=±5% resistance=13k package=THT]
  R7 = Resistor [tolerance=±5% resistance=13k package=THT]
  IC1 = IC, DIP package, 8 pins [chip_label=IC]
  Y1 = CRYSTAL [package=tc38h]
  LED5 = LED - 5mm [color="Red (633nm)" package="5 mm [THT]"]
  LED6 = LED - 5mm [color="Red (633nm)" package="5 mm [THT]"]
  LED7 = LED - 5mm [color="Red (633nm)" package="5 mm [THT]"]
  LED8 = LED - 5mm [color="Red (633nm)" package="5 mm [THT]"]
  LED9 = LED - 5mm [color="Red (633nm)" package="5 mm [THT]"]
  LED10 = LED - 5mm [color="Red (633nm)" package="5 mm [THT]"]
  LED11 = LED - 5mm [color="Red (633nm)" package="5 mm [THT]"]
  R8 = Resistor [tolerance=±5% resistance=13k package=THT]
  LED12 = LED - 5mm [color="Red (633nm)" package="5 mm [THT]"]
  R9 = Resistor [tolerance=±5% resistance=13k package=THT]
  LED13 = LED - 5mm [color="Red (633nm)" package="5 mm [THT]"]
  R10 = Resistor [tolerance=±5% resistance=13k package=THT]
  LED14 = LED - 5mm [color="Red (633nm)" package="5 mm [THT]"]
  R11 = Resistor [tolerance=±5% resistance=13k package=THT]

nets:
  N1: Raspberry_Pi_1.3v3, IC1.pin8
  N2: Raspberry_Pi_1.GPIO2, IC1.pin5
  N3: Raspberry_Pi_1.GPIO3, IC1.pin6
  N4: Raspberry_Pi_1.GPIO4, S2.Pin_1, S2.Pin_2
  N5: Raspberry_Pi_1.GPIO17, S1.Pin_1, S1.Pin_2
  N6: Raspberry_Pi_1.GPIO22, LED12.anode
  N7: Raspberry_Pi_1.GPIO5, LED9.anode
  N8: Raspberry_Pi_1.GPIO6, LED7.anode
  N9: Raspberry_Pi_1.GPIO13, LED4.anode
  N10: Raspberry_Pi_1.GPIO26, LED6.anode
  N11: Raspberry_Pi_1.GPIO16, LED5.anode
  N12: Raspberry_Pi_1.GPIO12, LED8.anode
  N13: Raspberry_Pi_1.GPIO25, LED10.anode
  N14: Raspberry_Pi_1.GPIO24, LED11.anode
  N15: Raspberry_Pi_1.GPIO23, LED13.anode
  N16: Raspberry_Pi_1.GPIO18, LED14.anode
  N17: Raspberry_Pi_1.GND, S1.Pin_3, S1.Pin_4, S2.Pin_3, S2.Pin_4, R1.Pin_1, R2.Pin_1, R3.Pin_1, R4.Pin_1, R5.Pin_1, R6.Pin_1, R7.Pin_1, IC1.pin4, R8.Pin_1, R9.Pin_1, R10.Pin_1, R11.Pin_1
  N18: C1.0, IC1.pin1, Y1.1
  N19: C1.1, IC1.pin2, Y1.2
  N20: R1.Pin_0, LED7.cathode
  N21: R2.Pin_0, LED6.cathode
  N22: R3.Pin_0, LED5.cathode
  N23: LED4.cathode, R4.Pin_0
  N24: R5.Pin_0, LED8.cathode
  N25: R6.Pin_0, LED9.cathode
  N26: R7.Pin_0, LED10.cathode
  N27: LED11.cathode, R11.Pin_0
  N28: R8.Pin_0, LED12.cathode
  N29: R9.Pin_0, LED13.cathode
  N30: R10.Pin_0, LED14.cathode
